// Logisim project 189 stuff.circ as structural Verilog: 2 circuits, main circuit main
module main (
  input  in_1,
  output [3:0] out_2
);

  wire clock_1_out, not_1_out, or_1_out, or_2_out;
  wire [7:0] counter_1_q, rom_1_data;

  Clock clock_1 (.out(clock_1_out));
  Counter counter_1 (.Q(counter_1_q), .clk(clock_1_out), .clr(in_1));  // open: load, D, count, carry
  ROM rom_1 (.addr(counter_1_q), .data(rom_1_data));  // open: sel
  not not_1 (not_1_out, or_1_out);
  or or_1 (or_1_out, rom_1_data[0], rom_1_data[1], rom_1_data[2], rom_1_data[3]);
  _74ls189 u_74ls189_1 (.data_in(rom_1_data[3:0]), .a_in(rom_1_data[7:4]), .clear(in_1), .we(or_2_out), .out_5(out_2));
  or or_2 (or_2_out, not_1_out, clock_1_out);

  // Notes on the sheet:
  //   contents of rom_1 (hex, n*v repeats v):
  //   1 12 24 38 0 10 20 30
endmodule

module _74ls189 (
  input  [3:0] data_in,
  input  [3:0] a_in,
  input  clear,
  input  we,
  output [3:0] out_5
);

  wire d_ff_1_q, d_ff_2_q, d_ff_3_q, d_ff_4_q, d_ff_5_q, d_ff_6_q, d_ff_7_q, d_ff_8_q, d_ff_9_q, d_ff_10_q,
       d_ff_11_q, d_ff_12_q, d_ff_13_q, d_ff_14_q, d_ff_15_q, d_ff_16_q, d_ff_17_q, d_ff_18_q, d_ff_19_q,
       d_ff_20_q, d_ff_21_q, d_ff_22_q, d_ff_23_q, d_ff_24_q, d_ff_25_q, d_ff_26_q, d_ff_27_q, d_ff_28_q,
       d_ff_29_q, d_ff_30_q, d_ff_31_q, d_ff_32_q, d_ff_33_q, d_ff_34_q, d_ff_35_q, d_ff_36_q, d_ff_37_q,
       d_ff_38_q, d_ff_39_q, d_ff_40_q, d_ff_41_q, d_ff_42_q, d_ff_43_q, d_ff_44_q, d_ff_45_q, d_ff_46_q,
       d_ff_47_q, d_ff_48_q, d_ff_49_q, d_ff_50_q, d_ff_51_q, d_ff_52_q, d_ff_53_q, d_ff_54_q, d_ff_55_q,
       d_ff_56_q, d_ff_57_q, d_ff_58_q, d_ff_59_q, d_ff_60_q, d_ff_61_q, d_ff_62_q, d_ff_63_q, d_ff_64_q,
       decoder_1_out0, decoder_1_out1, decoder_1_out2, decoder_1_out3, decoder_1_out4, decoder_1_out5,
       decoder_1_out6, decoder_1_out7, decoder_1_out8, decoder_1_out9, decoder_1_out10, decoder_1_out11,
       decoder_1_out12, decoder_1_out13, decoder_1_out14, decoder_1_out15, not_1_out;
  wire [3:0] buffer_1_out;

  Decoder #(.select(4), .enable("false")) decoder_1 (
    .out0(decoder_1_out0), .out1(decoder_1_out1), .out2(decoder_1_out2), .out3(decoder_1_out3),
    .out4(decoder_1_out4), .out5(decoder_1_out5), .out6(decoder_1_out6), .out7(decoder_1_out7),
    .out8(decoder_1_out8), .out9(decoder_1_out9), .out10(decoder_1_out10), .out11(decoder_1_out11),
    .out12(decoder_1_out12), .out13(decoder_1_out13), .out14(decoder_1_out14), .out15(decoder_1_out15),
    .sel(a_in));
  not not_1 (not_1_out, we);
  buf buffer_1 (buffer_1_out[0], d_ff_1_q);
  D_Flip_Flop #(.trigger("high")) d_ff_1 (
    .clk(not_1_out), .D(data_in[0]), .Q(d_ff_1_q), .en(decoder_1_out0), .reset(clear));  // open: Qn, preset
  buf buffer_2 (buffer_1_out[0], d_ff_2_q);
  D_Flip_Flop #(.trigger("high")) d_ff_2 (
    .clk(not_1_out), .D(data_in[0]), .Q(d_ff_2_q), .en(decoder_1_out1), .reset(clear));  // open: Qn, preset
  buf buffer_3 (buffer_1_out[0], d_ff_3_q);
  D_Flip_Flop #(.trigger("high")) d_ff_3 (
    .clk(not_1_out), .D(data_in[0]), .Q(d_ff_3_q), .en(decoder_1_out2), .reset(clear));  // open: Qn, preset
  buf buffer_4 (buffer_1_out[0], d_ff_4_q);
  D_Flip_Flop #(.trigger("high")) d_ff_4 (
    .clk(not_1_out), .D(data_in[0]), .Q(d_ff_4_q), .en(decoder_1_out3), .reset(clear));  // open: Qn, preset
  buf buffer_5 (buffer_1_out[0], d_ff_5_q);
  D_Flip_Flop #(.trigger("high")) d_ff_5 (
    .clk(not_1_out), .D(data_in[0]), .Q(d_ff_5_q), .en(decoder_1_out4), .reset(clear));  // open: Qn, preset
  buf buffer_6 (buffer_1_out[0], d_ff_6_q);
  D_Flip_Flop #(.trigger("high")) d_ff_6 (
    .clk(not_1_out), .D(data_in[0]), .Q(d_ff_6_q), .en(decoder_1_out5), .reset(clear));  // open: Qn, preset
  D_Flip_Flop #(.trigger("high")) d_ff_7 (
    .clk(not_1_out), .D(data_in[0]), .Q(d_ff_7_q), .en(decoder_1_out6), .reset(clear));  // open: Qn, preset
  buf buffer_7 (buffer_1_out[0], d_ff_7_q);
  D_Flip_Flop #(.trigger("high")) d_ff_8 (
    .clk(not_1_out), .D(data_in[0]), .Q(d_ff_8_q), .en(decoder_1_out7), .reset(clear));  // open: Qn, preset
  buf buffer_8 (buffer_1_out[0], d_ff_8_q);
  D_Flip_Flop #(.trigger("high")) d_ff_9 (
    .clk(not_1_out), .D(data_in[0]), .Q(d_ff_9_q), .en(decoder_1_out8), .reset(clear));  // open: Qn, preset
  buf buffer_9 (buffer_1_out[0], d_ff_9_q);
  buf buffer_10 (buffer_1_out[0], d_ff_10_q);
  D_Flip_Flop #(.trigger("high")) d_ff_10 (
    .clk(not_1_out), .D(data_in[0]), .Q(d_ff_10_q), .en(decoder_1_out9), .reset(clear));  // open: Qn, preset
  D_Flip_Flop #(.trigger("high")) d_ff_11 (
    .clk(not_1_out), .D(data_in[0]), .Q(d_ff_11_q), .en(decoder_1_out10), .reset(clear));  // open: Qn, preset
  buf buffer_11 (buffer_1_out[0], d_ff_11_q);
  D_Flip_Flop #(.trigger("high")) d_ff_12 (
    .clk(not_1_out), .D(data_in[0]), .Q(d_ff_12_q), .en(decoder_1_out11), .reset(clear));  // open: Qn, preset
  buf buffer_12 (buffer_1_out[0], d_ff_12_q);
  buf buffer_13 (buffer_1_out[0], d_ff_13_q);
  D_Flip_Flop #(.trigger("high")) d_ff_13 (
    .clk(not_1_out), .D(data_in[0]), .Q(d_ff_13_q), .en(decoder_1_out12), .reset(clear));  // open: Qn, preset
  D_Flip_Flop #(.trigger("high")) d_ff_14 (
    .clk(not_1_out), .D(data_in[0]), .Q(d_ff_14_q), .en(decoder_1_out13), .reset(clear));  // open: Qn, preset
  buf buffer_14 (buffer_1_out[0], d_ff_14_q);
  buf buffer_15 (buffer_1_out[0], d_ff_15_q);
  D_Flip_Flop #(.trigger("high")) d_ff_15 (
    .clk(not_1_out), .D(data_in[0]), .Q(d_ff_15_q), .en(decoder_1_out14), .reset(clear));  // open: Qn, preset
  D_Flip_Flop #(.trigger("high")) d_ff_16 (
    .clk(not_1_out), .D(data_in[0]), .Q(d_ff_16_q), .en(decoder_1_out15), .reset(clear));  // open: Qn, preset
  buf buffer_16 (buffer_1_out[0], d_ff_16_q);
  D_Flip_Flop #(.trigger("high")) d_ff_17 (
    .clk(not_1_out), .D(data_in[1]), .Q(d_ff_17_q), .en(decoder_1_out0), .reset(clear));  // open: Qn, preset
  buf buffer_17 (buffer_1_out[1], d_ff_17_q);
  D_Flip_Flop #(.trigger("high")) d_ff_18 (
    .clk(not_1_out), .D(data_in[1]), .Q(d_ff_18_q), .en(decoder_1_out1), .reset(clear));  // open: Qn, preset
  buf buffer_18 (buffer_1_out[1], d_ff_18_q);
  D_Flip_Flop #(.trigger("high")) d_ff_19 (
    .clk(not_1_out), .D(data_in[1]), .Q(d_ff_19_q), .en(decoder_1_out2), .reset(clear));  // open: Qn, preset
  buf buffer_19 (buffer_1_out[1], d_ff_19_q);
  buf buffer_20 (buffer_1_out[1], d_ff_20_q);
  D_Flip_Flop #(.trigger("high")) d_ff_20 (
    .clk(not_1_out), .D(data_in[1]), .Q(d_ff_20_q), .en(decoder_1_out3), .reset(clear));  // open: Qn, preset
  buf buffer_21 (buffer_1_out[1], d_ff_21_q);
  D_Flip_Flop #(.trigger("high")) d_ff_21 (
    .clk(not_1_out), .D(data_in[1]), .Q(d_ff_21_q), .en(decoder_1_out4), .reset(clear));  // open: Qn, preset
  D_Flip_Flop #(.trigger("high")) d_ff_22 (
    .clk(not_1_out), .D(data_in[1]), .Q(d_ff_22_q), .en(decoder_1_out5), .reset(clear));  // open: Qn, preset
  buf buffer_22 (buffer_1_out[1], d_ff_22_q);
  buf buffer_23 (buffer_1_out[1], d_ff_23_q);
  D_Flip_Flop #(.trigger("high")) d_ff_23 (
    .clk(not_1_out), .D(data_in[1]), .Q(d_ff_23_q), .en(decoder_1_out6), .reset(clear));  // open: Qn, preset
  buf buffer_24 (buffer_1_out[1], d_ff_24_q);
  D_Flip_Flop #(.trigger("high")) d_ff_24 (
    .clk(not_1_out), .D(data_in[1]), .Q(d_ff_24_q), .en(decoder_1_out7), .reset(clear));  // open: Qn, preset
  buf buffer_25 (buffer_1_out[1], d_ff_25_q);
  D_Flip_Flop #(.trigger("high")) d_ff_25 (
    .clk(not_1_out), .D(data_in[1]), .Q(d_ff_25_q), .en(decoder_1_out8), .reset(clear));  // open: Qn, preset
  D_Flip_Flop #(.trigger("high")) d_ff_26 (
    .clk(not_1_out), .D(data_in[1]), .Q(d_ff_26_q), .en(decoder_1_out9), .reset(clear));  // open: Qn, preset
  buf buffer_26 (buffer_1_out[1], d_ff_26_q);
  buf buffer_27 (buffer_1_out[1], d_ff_27_q);
  D_Flip_Flop #(.trigger("high")) d_ff_27 (
    .clk(not_1_out), .D(data_in[1]), .Q(d_ff_27_q), .en(decoder_1_out10), .reset(clear));  // open: Qn, preset
  buf buffer_28 (buffer_1_out[1], d_ff_28_q);
  D_Flip_Flop #(.trigger("high")) d_ff_28 (
    .clk(not_1_out), .D(data_in[1]), .Q(d_ff_28_q), .en(decoder_1_out11), .reset(clear));  // open: Qn, preset
  buf buffer_29 (buffer_1_out[1], d_ff_29_q);
  D_Flip_Flop #(.trigger("high")) d_ff_29 (
    .clk(not_1_out), .D(data_in[1]), .Q(d_ff_29_q), .en(decoder_1_out12), .reset(clear));  // open: Qn, preset
  buf buffer_30 (buffer_1_out[1], d_ff_30_q);
  D_Flip_Flop #(.trigger("high")) d_ff_30 (
    .clk(not_1_out), .D(data_in[1]), .Q(d_ff_30_q), .en(decoder_1_out13), .reset(clear));  // open: Qn, preset
  buf buffer_31 (buffer_1_out[1], d_ff_31_q);
  D_Flip_Flop #(.trigger("high")) d_ff_31 (
    .clk(not_1_out), .D(data_in[1]), .Q(d_ff_31_q), .en(decoder_1_out14), .reset(clear));  // open: Qn, preset
  D_Flip_Flop #(.trigger("high")) d_ff_32 (
    .clk(not_1_out), .D(data_in[1]), .Q(d_ff_32_q), .en(decoder_1_out15), .reset(clear));  // open: Qn, preset
  buf buffer_32 (buffer_1_out[1], d_ff_32_q);
  buf buffer_33 (buffer_1_out[2], d_ff_33_q);
  D_Flip_Flop #(.trigger("high")) d_ff_33 (
    .clk(not_1_out), .D(data_in[2]), .Q(d_ff_33_q), .en(decoder_1_out0), .reset(clear));  // open: Qn, preset
  buf buffer_34 (buffer_1_out[2], d_ff_34_q);
  D_Flip_Flop #(.trigger("high")) d_ff_34 (
    .clk(not_1_out), .D(data_in[2]), .Q(d_ff_34_q), .en(decoder_1_out1), .reset(clear));  // open: Qn, preset
  buf buffer_35 (buffer_1_out[2], d_ff_35_q);
  D_Flip_Flop #(.trigger("high")) d_ff_35 (
    .clk(not_1_out), .D(data_in[2]), .Q(d_ff_35_q), .en(decoder_1_out2), .reset(clear));  // open: Qn, preset
  D_Flip_Flop #(.trigger("high")) d_ff_36 (
    .clk(not_1_out), .D(data_in[2]), .Q(d_ff_36_q), .en(decoder_1_out3), .reset(clear));  // open: Qn, preset
  buf buffer_36 (buffer_1_out[2], d_ff_36_q);
  D_Flip_Flop #(.trigger("high")) d_ff_37 (
    .clk(not_1_out), .D(data_in[2]), .Q(d_ff_37_q), .en(decoder_1_out4), .reset(clear));  // open: Qn, preset
  buf buffer_37 (buffer_1_out[2], d_ff_37_q);
  D_Flip_Flop #(.trigger("high")) d_ff_38 (
    .clk(not_1_out), .D(data_in[2]), .Q(d_ff_38_q), .en(decoder_1_out5), .reset(clear));  // open: Qn, preset
  buf buffer_38 (buffer_1_out[2], d_ff_38_q);
  D_Flip_Flop #(.trigger("high")) d_ff_39 (
    .clk(not_1_out), .D(data_in[2]), .Q(d_ff_39_q), .en(decoder_1_out6), .reset(clear));  // open: Qn, preset
  buf buffer_39 (buffer_1_out[2], d_ff_39_q);
  buf buffer_40 (buffer_1_out[2], d_ff_40_q);
  D_Flip_Flop #(.trigger("high")) d_ff_40 (
    .clk(not_1_out), .D(data_in[2]), .Q(d_ff_40_q), .en(decoder_1_out7), .reset(clear));  // open: Qn, preset
  D_Flip_Flop #(.trigger("high")) d_ff_41 (
    .clk(not_1_out), .D(data_in[2]), .Q(d_ff_41_q), .en(decoder_1_out8), .reset(clear));  // open: Qn, preset
  buf buffer_41 (buffer_1_out[2], d_ff_41_q);
  D_Flip_Flop #(.trigger("high")) d_ff_42 (
    .clk(not_1_out), .D(data_in[2]), .Q(d_ff_42_q), .en(decoder_1_out9), .reset(clear));  // open: Qn, preset
  buf buffer_42 (buffer_1_out[2], d_ff_42_q);
  D_Flip_Flop #(.trigger("high")) d_ff_43 (
    .clk(not_1_out), .D(data_in[2]), .Q(d_ff_43_q), .en(decoder_1_out10), .reset(clear));  // open: Qn, preset
  buf buffer_43 (buffer_1_out[2], d_ff_43_q);
  D_Flip_Flop #(.trigger("high")) d_ff_44 (
    .clk(not_1_out), .D(data_in[2]), .Q(d_ff_44_q), .en(decoder_1_out11), .reset(clear));  // open: Qn, preset
  buf buffer_44 (buffer_1_out[2], d_ff_44_q);
  buf buffer_45 (buffer_1_out[2], d_ff_45_q);
  D_Flip_Flop #(.trigger("high")) d_ff_45 (
    .clk(not_1_out), .D(data_in[2]), .Q(d_ff_45_q), .en(decoder_1_out12), .reset(clear));  // open: Qn, preset
  D_Flip_Flop #(.trigger("high")) d_ff_46 (
    .clk(not_1_out), .D(data_in[2]), .Q(d_ff_46_q), .en(decoder_1_out13), .reset(clear));  // open: Qn, preset
  buf buffer_46 (buffer_1_out[2], d_ff_46_q);
  buf buffer_47 (buffer_1_out[2], d_ff_47_q);
  D_Flip_Flop #(.trigger("high")) d_ff_47 (
    .clk(not_1_out), .D(data_in[2]), .Q(d_ff_47_q), .en(decoder_1_out14), .reset(clear));  // open: Qn, preset
  D_Flip_Flop #(.trigger("high")) d_ff_48 (
    .clk(not_1_out), .D(data_in[2]), .Q(d_ff_48_q), .en(decoder_1_out15), .reset(clear));  // open: Qn, preset
  buf buffer_48 (buffer_1_out[2], d_ff_48_q);
  D_Flip_Flop #(.trigger("high")) d_ff_49 (
    .clk(not_1_out), .D(data_in[3]), .Q(d_ff_49_q), .en(decoder_1_out0), .reset(clear));  // open: Qn, preset
  D_Flip_Flop #(.trigger("high")) d_ff_50 (
    .clk(not_1_out), .D(data_in[3]), .Q(d_ff_50_q), .en(decoder_1_out1), .reset(clear));  // open: Qn, preset
  D_Flip_Flop #(.trigger("high")) d_ff_51 (
    .clk(not_1_out), .D(data_in[3]), .Q(d_ff_51_q), .en(decoder_1_out2), .reset(clear));  // open: Qn, preset
  D_Flip_Flop #(.trigger("high")) d_ff_52 (
    .clk(not_1_out), .D(data_in[3]), .Q(d_ff_52_q), .en(decoder_1_out3), .reset(clear));  // open: Qn, preset
  D_Flip_Flop #(.trigger("high")) d_ff_53 (
    .clk(not_1_out), .D(data_in[3]), .Q(d_ff_53_q), .en(decoder_1_out4), .reset(clear));  // open: Qn, preset
  D_Flip_Flop #(.trigger("high")) d_ff_54 (
    .clk(not_1_out), .D(data_in[3]), .Q(d_ff_54_q), .en(decoder_1_out5), .reset(clear));  // open: Qn, preset
  D_Flip_Flop #(.trigger("high")) d_ff_55 (
    .clk(not_1_out), .D(data_in[3]), .Q(d_ff_55_q), .en(decoder_1_out6), .reset(clear));  // open: Qn, preset
  D_Flip_Flop #(.trigger("high")) d_ff_56 (
    .clk(not_1_out), .D(data_in[3]), .Q(d_ff_56_q), .en(decoder_1_out7), .reset(clear));  // open: Qn, preset
  D_Flip_Flop #(.trigger("high")) d_ff_57 (
    .clk(not_1_out), .D(data_in[3]), .Q(d_ff_57_q), .en(decoder_1_out8), .reset(clear));  // open: Qn, preset
  D_Flip_Flop #(.trigger("high")) d_ff_58 (
    .clk(not_1_out), .D(data_in[3]), .Q(d_ff_58_q), .en(decoder_1_out9), .reset(clear));  // open: Qn, preset
  D_Flip_Flop #(.trigger("high")) d_ff_59 (
    .clk(not_1_out), .D(data_in[3]), .Q(d_ff_59_q), .en(decoder_1_out10), .reset(clear));  // open: Qn, preset
  D_Flip_Flop #(.trigger("high")) d_ff_60 (
    .clk(not_1_out), .D(data_in[3]), .Q(d_ff_60_q), .en(decoder_1_out11), .reset(clear));  // open: Qn, preset
  D_Flip_Flop #(.trigger("high")) d_ff_61 (
    .clk(not_1_out), .D(data_in[3]), .Q(d_ff_61_q), .en(decoder_1_out12), .reset(clear));  // open: Qn, preset
  D_Flip_Flop #(.trigger("high")) d_ff_62 (
    .clk(not_1_out), .D(data_in[3]), .Q(d_ff_62_q), .en(decoder_1_out13), .reset(clear));  // open: Qn, preset
  D_Flip_Flop #(.trigger("high")) d_ff_63 (
    .clk(not_1_out), .D(data_in[3]), .Q(d_ff_63_q), .en(decoder_1_out14), .reset(clear));  // open: Qn, preset
  D_Flip_Flop #(.trigger("high")) d_ff_64 (
    .clk(not_1_out), .D(data_in[3]), .Q(d_ff_64_q), .en(decoder_1_out15), .reset(clear));  // open: Qn, preset
  buf buffer_49 (buffer_1_out[3], d_ff_49_q);
  buf buffer_50 (buffer_1_out[3], d_ff_50_q);
  buf buffer_51 (buffer_1_out[3], d_ff_51_q);
  buf buffer_52 (buffer_1_out[3], d_ff_52_q);
  buf buffer_53 (buffer_1_out[3], d_ff_53_q);
  buf buffer_54 (buffer_1_out[3], d_ff_54_q);
  buf buffer_55 (buffer_1_out[3], d_ff_55_q);
  buf buffer_56 (buffer_1_out[3], d_ff_56_q);
  buf buffer_57 (buffer_1_out[3], d_ff_57_q);
  buf buffer_58 (buffer_1_out[3], d_ff_58_q);
  buf buffer_59 (buffer_1_out[3], d_ff_59_q);
  buf buffer_60 (buffer_1_out[3], d_ff_60_q);
  buf buffer_61 (buffer_1_out[3], d_ff_61_q);
  buf buffer_62 (buffer_1_out[3], d_ff_62_q);
  buf buffer_63 (buffer_1_out[3], d_ff_63_q);
  buf buffer_64 (buffer_1_out[3], d_ff_64_q);
  Pull_Resistor pull_resistor_1 (.node(buffer_1_out));
  assign out_5 = ~buffer_1_out;  // NOT_Gate not_2, 4 bits wide

  // Notes on the sheet:
  //   buffer_1 drives only 1 and floats otherwise
  //   buffer_2 drives only 1 and floats otherwise
  //   buffer_3 drives only 1 and floats otherwise
  //   buffer_4 drives only 1 and floats otherwise
  //   buffer_5 drives only 1 and floats otherwise
  //   buffer_6 drives only 1 and floats otherwise
  //   buffer_7 drives only 1 and floats otherwise
  //   buffer_8 drives only 1 and floats otherwise
  //   buffer_9 drives only 1 and floats otherwise
  //   buffer_10 drives only 1 and floats otherwise
  //   buffer_11 drives only 1 and floats otherwise
  //   buffer_12 drives only 1 and floats otherwise
  //   buffer_13 drives only 1 and floats otherwise
  //   buffer_14 drives only 1 and floats otherwise
  //   buffer_15 drives only 1 and floats otherwise
  //   buffer_16 drives only 1 and floats otherwise
  //   buffer_17 drives only 1 and floats otherwise
  //   buffer_18 drives only 1 and floats otherwise
  //   buffer_19 drives only 1 and floats otherwise
  //   buffer_20 drives only 1 and floats otherwise
  //   buffer_21 drives only 1 and floats otherwise
  //   buffer_22 drives only 1 and floats otherwise
  //   buffer_23 drives only 1 and floats otherwise
  //   buffer_24 drives only 1 and floats otherwise
  //   buffer_25 drives only 1 and floats otherwise
  //   buffer_26 drives only 1 and floats otherwise
  //   buffer_27 drives only 1 and floats otherwise
  //   buffer_28 drives only 1 and floats otherwise
  //   buffer_29 drives only 1 and floats otherwise
  //   buffer_30 drives only 1 and floats otherwise
  //   buffer_31 drives only 1 and floats otherwise
  //   buffer_32 drives only 1 and floats otherwise
  //   buffer_33 drives only 1 and floats otherwise
  //   buffer_34 drives only 1 and floats otherwise
  //   buffer_35 drives only 1 and floats otherwise
  //   buffer_36 drives only 1 and floats otherwise
  //   buffer_37 drives only 1 and floats otherwise
  //   buffer_38 drives only 1 and floats otherwise
  //   buffer_39 drives only 1 and floats otherwise
  //   buffer_40 drives only 1 and floats otherwise
  //   buffer_41 drives only 1 and floats otherwise
  //   buffer_42 drives only 1 and floats otherwise
  //   buffer_43 drives only 1 and floats otherwise
  //   buffer_44 drives only 1 and floats otherwise
  //   buffer_45 drives only 1 and floats otherwise
  //   buffer_46 drives only 1 and floats otherwise
  //   buffer_47 drives only 1 and floats otherwise
  //   buffer_48 drives only 1 and floats otherwise
  //   buffer_49 drives only 1 and floats otherwise
  //   buffer_50 drives only 1 and floats otherwise
  //   buffer_51 drives only 1 and floats otherwise
  //   buffer_52 drives only 1 and floats otherwise
  //   buffer_53 drives only 1 and floats otherwise
  //   buffer_54 drives only 1 and floats otherwise
  //   buffer_55 drives only 1 and floats otherwise
  //   buffer_56 drives only 1 and floats otherwise
  //   buffer_57 drives only 1 and floats otherwise
  //   buffer_58 drives only 1 and floats otherwise
  //   buffer_59 drives only 1 and floats otherwise
  //   buffer_60 drives only 1 and floats otherwise
  //   buffer_61 drives only 1 and floats otherwise
  //   buffer_62 drives only 1 and floats otherwise
  //   buffer_63 drives only 1 and floats otherwise
  //   buffer_64 drives only 1 and floats otherwise
endmodule
