// Logisim project 189 become shift register.circ as structural Verilog: 1 circuit, main circuit main
module main (
  input  [3:0] in_1,
  input  in_2,
  input  in_3,
  input  in_4,
  output [3:0] out_5
);

  wire [3:0] ram_1_data, register_1_q;

  Register #(.width(4), .trigger("high")) register_1 (.D(out_5), .Q(register_1_q), .clk(in_3));  // open: en, clr
  RAM #(.addrWidth(4), .dataWidth(4), .bus("separate")) ram_1 (
    .addr(in_1), .din(register_1_q), .data(ram_1_data), .str(in_2), .sel(1'b1), .clk(in_3), .ld(1'b1),
    .clr(in_4));
  assign out_5 = ~ram_1_data;  // NOT_Gate not_1, 4 bits wide
endmodule
